// Logisim project cpu-circuit.circ as structural Verilog: 1 circuit, main circuit main
module main (
);

  wire and_1_out, and_3_out, CARR_BIT, CARRY_FLAG, CLK, clock_1_out, COUNT_ENABLE, DISP_REG_WRITE, EO,
       FLAG_REG_WRITE, JUMP, MEM_READ, MEM_WRITE, n7_segment_display_1_p1, n7_segment_display_2_p1,
       n7_segment_display_3_p1, n7_segment_display_4_p1, n7_segment_display_5_p1, n7_segment_display_6_p1,
       not_1_out, not_2_out, not_3_out, not_4_out, not_5_out, PRG_CNT_READ, REG_A_READ, REG_A_WRITE,
       REG_B_WRITE, REG_INS_READ, REG_INS_WRITE, REG_MEMADDR_WRITE, STOP, SUB, ZERO_FLAG;
  wire [1:0] controlled_buffer_9_out;
  wire [3:0] buffer_1_out, buffer_10_out, controlled_buffer_8_out, controlled_buffer_10_out, counter_1_q,
       INS_DECODER, INSTR_REG_q, INSTR_STEP_COUNTER_q;
  wire [7:0] ALU_IN_A, ALU_IN_B, ALU_VALUE, and_2_out, buffer_2_out, buffer_3_out, BUS_1, DISP_REG_q,
       MEM_ADDRESS_REG_q, ram_1_dout, xor_1_out;
  wire [7:2] register_1_q;
  wire [9:0] dipswitch_1_sw10;

  Clock clock_1 (.out(clock_1_out));
  not not_1 (not_1_out, STOP);
  assign CLK = not_1_out ? clock_1_out : 1'bz;  // Controlled_Buffer controlled_buffer_1
  Register A_Reg (.D(BUS_1), .en(REG_A_WRITE), .clk(CLK), .Q(ALU_IN_A));  // open: clr
  not not_2 (not_2_out, REG_A_WRITE);
  and and_1 (and_1_out, not_2_out, REG_A_READ);
  assign BUS_1 = and_1_out ? ALU_IN_A : 8'bz;  // Controlled_Buffer controlled_buffer_2
  // Probe on ALU_IN_A
  Counter #(.max('hf), .width(4)) counter_1 (
    .load(JUMP), .count(COUNT_ENABLE), .clk(CLK), .D(BUS_1[3:0]), .Q(counter_1_q));  // open: clr, up, carry
  xor xor_1 (xor_1_out[0], SUB, ALU_IN_B[0]);
  xor xor_2 (xor_1_out[1], SUB, ALU_IN_B[1]);
  xor xor_3 (xor_1_out[2], SUB, ALU_IN_B[2]);
  xor xor_4 (xor_1_out[3], SUB, ALU_IN_B[3]);
  xor xor_5 (xor_1_out[4], SUB, ALU_IN_B[4]);
  xor xor_6 (xor_1_out[5], SUB, ALU_IN_B[5]);
  xor xor_7 (xor_1_out[6], SUB, ALU_IN_B[6]);
  xor xor_8 (xor_1_out[7], SUB, ALU_IN_B[7]);
  assign buffer_1_out = 4'b0000;  // Buffer buffer_1, 4 bits wide
  Adder adder_1 (.a(xor_1_out), .b(ALU_IN_A), .out(ALU_VALUE), .cin(SUB), .cout(CARR_BIT));
  assign BUS_1 = PRG_CNT_READ ? {buffer_1_out, counter_1_q} : 8'bz;  // Controlled_Buffer controlled_buffer_3
  Register DISP_REG (.D(BUS_1), .en(DISP_REG_WRITE), .clk(CLK), .Q(DISP_REG_q));  // open: clr
  Register B_REG (.D(BUS_1), .en(REG_B_WRITE), .clk(CLK), .Q(ALU_IN_B));  // open: clr
  assign BUS_1 = EO ? ALU_VALUE : 8'bz;  // Controlled_Buffer controlled_buffer_4
  // Probe on BUS_1
  // Probe on BUS_1
  // _7_Segment_Display 7_segment_display_1: pin names not known; wires that end beside it: n7_segment_display_1_p1, n7_segment_display_1_p1
  // _7_Segment_Display 7_segment_display_2: pin names not known; wires that end beside it: n7_segment_display_2_p1, n7_segment_display_2_p1
  // BCD_to_7_Segment_decoder bcd_to_7_segment_decoder_1: pin names not known
  // BCD_to_7_Segment_decoder bcd_to_7_segment_decoder_2: pin names not known
  // Binary_to_BCD_converter #(.binvalue(8)) binary_to_bcd_converter_1: pin names not known; wires that end beside it: DISP_REG_q, BUS_1
  not not_3 (not_3_out, REG_B_WRITE);
  Controlled_Buffer #(.width(8)) controlled_buffer_5 (.in(ALU_IN_B), .en(not_3_out));  // open: out
  // Probe on ALU_IN_B
  // _7_Segment_Display 7_segment_display_3: pin names not known; wires that end beside it: n7_segment_display_3_p1, n7_segment_display_3_p1
  // BCD_to_7_Segment_decoder bcd_to_7_segment_decoder_3: pin names not known
  assign buffer_2_out = ALU_VALUE;  // Buffer buffer_2, 8 bits wide
  and and_2 (and_2_out[0], ~buffer_2_out[0], ~buffer_2_out[1], ~buffer_2_out[2], ~buffer_2_out[3], ~buffer_2_out[4], ~buffer_2_out[5], ~buffer_2_out[6], ~buffer_2_out[7]);  // AND_Gate
  assign buffer_3_out = BUS_1;  // Buffer buffer_3, 8 bits wide
  buf buffer_4 (and_2_out[2], 1'b0);
  buf buffer_5 (and_2_out[3], 1'b0);
  buf buffer_6 (and_2_out[4], 1'b0);
  buf buffer_7 (and_2_out[5], 1'b0);
  Register register_1 (
    .D({and_2_out[7:2], CARR_BIT, and_2_out[0]}), .en(FLAG_REG_WRITE), .clk(CLK),
    .Q({register_1_q, CARRY_FLAG, ZERO_FLAG}));  // open: clr
  buf buffer_8 (and_2_out[6], 1'b0);
  buf buffer_9 (and_2_out[7], 1'b0);
  LED led_1 (.in(buffer_3_out[7]));
  LED led_2 (.in(buffer_3_out[6]));
  LED led_3 (.in(buffer_3_out[5]));
  // _7_Segment_Display 7_segment_display_4: pin names not known; wires that end beside it: n7_segment_display_4_p1, n7_segment_display_4_p1
  // BCD_to_7_Segment_decoder bcd_to_7_segment_decoder_4: pin names not known
  // Binary_to_BCD_converter #(.binvalue(8)) binary_to_bcd_converter_2: pin names not known; wires that end beside it: buffer_3_out
  Register MEM_ADDRESS_REG (.D(BUS_1), .en(REG_MEMADDR_WRITE), .clk(CLK), .Q(MEM_ADDRESS_REG_q));  // open: clr
  LED led_4 (.in(buffer_3_out[4]));
  LED led_5 (.in(buffer_3_out[3]));
  LED led_6 (.in(buffer_3_out[2]));
  LED led_7 (.in(buffer_3_out[1]));
  // _7_Segment_Display 7_segment_display_5: pin names not known; wires that end beside it: n7_segment_display_5_p1, n7_segment_display_5_p1
  // _7_Segment_Display 7_segment_display_6: pin names not known; wires that end beside it: n7_segment_display_6_p1, n7_segment_display_6_p1
  // BCD_to_7_Segment_decoder bcd_to_7_segment_decoder_5: pin names not known
  // BCD_to_7_Segment_decoder bcd_to_7_segment_decoder_6: pin names not known
  Register INSTR_REG (.D(BUS_1), .en(REG_INS_WRITE), .clk(CLK), .Q({INS_DECODER, INSTR_REG_q}));  // open: clr
  // Probe on MEM_ADDRESS_REG_q
  LED led_8 (.in(buffer_3_out[0]));
  // Probe on INSTR_REG_q
  // Probe on {INS_DECODER, INSTR_REG_q}
  // Probe on MEM_ADDRESS_REG_q[3:0]
  not not_4 (not_4_out, REG_INS_WRITE);
  and and_3 (and_3_out, not_4_out, REG_INS_READ);
  assign buffer_10_out = 4'b0000;  // Buffer buffer_10, 4 bits wide
  assign BUS_1 = and_3_out ? {buffer_10_out, INSTR_REG_q} : 8'bz;  // Controlled_Buffer controlled_buffer_6
  // Probe on INS_DECODER
  RAM #(.addrWidth(4), .asyncread("true"), .\type ("nonvolatile")) ram_1 (
    .addr(MEM_ADDRESS_REG_q[3:0]), .we(MEM_WRITE), .clk(CLK), .din(BUS_1), .dout(ram_1_dout));  // open: oe
  Counter #(.max('h4), .width(4)) INSTR_STEP_COUNTER (
    .clk(CLK), .Q(INSTR_STEP_COUNTER_q));  // open: clr, load, up, count, D, carry
  assign BUS_1 = MEM_READ ? ram_1_dout : 8'bz;  // Controlled_Buffer controlled_buffer_7
  // Probe on ram_1_dout
  Decoder #(.enable("false"), .select(4)) decoder_1 (.sel(INSTR_STEP_COUNTER_q));  // open: out0, out1, out2, out3, out4, out5, out6, out7, out8, out9, out10, out11, out12, out13, out14, out15
  DipSwitch #(.number(10)) dipswitch_1 (
    .sw1(dipswitch_1_sw10[9]), .sw2(dipswitch_1_sw10[8]), .sw3(dipswitch_1_sw10[7]),
    .sw4(dipswitch_1_sw10[6]), .sw5(dipswitch_1_sw10[5]), .sw6(dipswitch_1_sw10[4]),
    .sw7(dipswitch_1_sw10[3]), .sw8(dipswitch_1_sw10[2]), .sw9(dipswitch_1_sw10[1]),
    .sw10(dipswitch_1_sw10[0]));
  assign controlled_buffer_8_out = 1'b1 ? INSTR_STEP_COUNTER_q : 4'bz;  // Controlled_Buffer controlled_buffer_8
  assign controlled_buffer_9_out = 1'b1 ? {ZERO_FLAG, CARRY_FLAG} : 2'bz;  // Controlled_Buffer controlled_buffer_9
  assign controlled_buffer_10_out = 1'b1 ? INS_DECODER : 4'bz;  // Controlled_Buffer controlled_buffer_10
  not not_5 (not_5_out, 1'b1);
  // Probe on {controlled_buffer_10_out, controlled_buffer_8_out, controlled_buffer_9_out}
  ROM #(.addrWidth(10), .dataWidth(16)) rom_1 (
    .addr({controlled_buffer_10_out, controlled_buffer_8_out, controlled_buffer_9_out}),
    .data({FLAG_REG_WRITE, REG_A_READ, REG_A_WRITE, REG_B_WRITE, REG_MEMADDR_WRITE, MEM_READ, EO, SUB, REG_INS_WRITE, REG_INS_READ, DISP_REG_WRITE, JUMP, STOP, COUNT_ENABLE, PRG_CNT_READ, MEM_WRITE}));
  assign {controlled_buffer_10_out, controlled_buffer_8_out, controlled_buffer_9_out} = not_5_out ? dipswitch_1_sw10 : 10'bz;  // Controlled_Buffer controlled_buffer_11

  // Other names for the same wires on the sheet: INV_CLK = CLK

  // Notes on the sheet:
  //   DISPLAY / OUTPUT
  //   BUS VALUE
  //   contents of rom_1 (hex, n*v repeats v):
  //   4*802 4*484 56*0 4*802 4*484 4*840 4*2400 48*0 4*802 4*484 4*840 4*1400 48*0 4*802 4*484 4*840
  //   4*1400 4*a200 44*0 4*802 4*484 4*840 4*1400 4*a300 44*0 4*802 4*484 4*4020 52*0 4*802 4*484 4*50
  //   52*0 4*802 4*484 4*840 4*4001 48*0 4*802 4*484 4*2040 52*0 4*802 4*484 0 0 50 50 52*0 4*802 4*484 0
  //   50 0 50 52*0 4*802 4*484 4*8 52*0 4*802 4*484 56*0 4*802 4*484 56*0 4*802 4*484 56*0 4*802 4*484
endmodule
